# Fritzing sketch led_cube (saved by Fritzing 0.7.5b)
perfboards: 2

parts:
  J1 = female pin header, 1 pin [form="♀ (female)"]
  J2 = female pin header, 1 pin [form="♀ (female)"]
  J3 = female pin header, 1 pin [form="♀ (female)"]
  J4 = female pin header, 1 pin [form="♀ (female)"]
  J5 = female pin header, 1 pin [form="♀ (female)"]
  J6 = female pin header, 1 pin [form="♀ (female)"]
  J7 = female pin header, 1 pin [form="♀ (female)"]
  J8 = female pin header, 1 pin [form="♀ (female)"]
  J9 = female pin header, 1 pin [form="♀ (female)"]
  J10 = female pin header, 1 pin [form="♀ (female)"]
  J11 = female pin header, 1 pin [form="♀ (female)"]
  J12 = female pin header, 1 pin [form="♀ (female)"]
  J13 = female pin header, 1 pin [form="♀ (female)"]
  J14 = female pin header, 1 pin [form="♀ (female)"]
  J15 = female pin header, 1 pin [form="♀ (female)"]
  J16 = female pin header, 1 pin [form="♀ (female)"]
  R1 = Resistor [tolerance=±5% resistance=220 package=THT]
  R2 = Resistor [tolerance=±5% resistance=220 package=THT]
  R3 = Resistor [tolerance=±5% resistance=220 package=THT]
  R4 = Resistor [tolerance=±5% resistance=220 package=THT]
  R5 = Resistor [tolerance=±5% resistance=220 package=THT]
  R6 = Resistor [tolerance=±5% resistance=220 package=THT]
  R7 = Resistor [tolerance=±5% resistance=220 package=THT]
  R8 = Resistor [tolerance=±5% resistance=220 package=THT]
  R9 = Resistor [tolerance=±5% resistance=220 package=THT]
  R10 = Resistor [tolerance=±5% resistance=220 package=THT]
  R11 = Resistor [tolerance=±5% resistance=220 package=THT]
  R12 = Resistor [tolerance=±5% resistance=220 package=THT]
  R13 = Resistor [tolerance=±5% resistance=220 package=THT]
  R14 = Resistor [tolerance=±5% resistance=220 package=THT]
  R15 = Resistor [tolerance=±5% resistance=220 package=THT]
  R16 = Resistor [tolerance=±5% resistance=220 package=THT]
  J17 = female pin header, 1 pin [form="♀ (female)"]  # not connected
  J18 = female pin header, 1 pin [form="♀ (female)"]  # not connected
  J19 = female pin header, 1 pin [form="♀ (female)"]  # not connected
  J20 = female pin header, 1 pin [form="♀ (female)"]  # not connected
  J21 = female pin header, 8 pins [form="♀ (female)"]  # not connected
  J23 = female pin header, 8 pins [form="♀ (female)"]  # not connected
  J22 = female pin header, 4 pins [form="♀ (female)"]
  U1 = atmega328 [package=dip]
  U2 = 74HC595 [package="DIP16 [THT]"]
  U3 = 74HC595 [package="DIP16 [THT]"]
  C1 = Ceramic Capacitor [capacitance=0.1µF package="100 mil [THT, multilayer]"]  # not connected
  R17 = Resistor [tolerance=±5% resistance=1k package=THT]
  B0 = female pin header, 1 pin [form="♀ (female)"]
  B1 = female pin header, 1 pin [form="♀ (female)"]
  B2 = female pin header, 1 pin [form="♀ (female)"]
  B3 = female pin header, 1 pin [form="♀ (female)"]
  B4 = female pin header, 1 pin [form="♀ (female)"]
  B5 = female pin header, 1 pin [form="♀ (female)"]
  B6 = female pin header, 1 pin [form="♀ (female)"]
  B7 = female pin header, 1 pin [form="♀ (female)"]
  B11 = female pin header, 1 pin [form="♀ (female)"]
  B13 = female pin header, 1 pin [form="♀ (female)"]
  B10 = female pin header, 1 pin [form="♀ (female)"]
  B8 = female pin header, 1 pin [form="♀ (female)"]
  B14 = female pin header, 1 pin [form="♀ (female)"]
  B9 = female pin header, 1 pin [form="♀ (female)"]
  B12 = female pin header, 1 pin [form="♀ (female)"]
  B15 = female pin header, 1 pin [form="♀ (female)"]
  C2 = Ceramic Capacitor [capacitance=0.1µF package="100 mil [THT, multilayer]"]
  Q1 = NPN-Transistor [package="TO92 [THT]"]
  Q2 = NPN-Transistor [package="TO92 [THT]"]
  Q3 = NPN-Transistor [package="TO92 [THT]"]
  Q4 = NPN-Transistor [package="TO92 [THT]"]
  R18 = Resistor [tolerance=±5% resistance=10k package=THT]
  R19 = Resistor [tolerance=±5% resistance=10k package=THT]
  R20 = Resistor [tolerance=±5% resistance=10k package=THT]
  R21 = Resistor [tolerance=±5% resistance=10k package=THT]
  R22 = Resistor [tolerance=±5% resistance=10k package=THT]  # not connected
  R23 = Resistor [tolerance=±5% resistance=10k package=THT]  # not connected
  R24 = Resistor [tolerance=±5% resistance=10k package=THT]  # not connected
  R25 = Resistor [tolerance=±5% resistance=10k package=THT]  # not connected
  J24 = female pin header, 10 pins [form="♀ (female)"]
  Q5 = Basic FET P-Channel [package="TO220 [THT]"]
  R26 = Resistor [tolerance=±5% resistance=3.3k package=THT]  # not connected
  R27 = Resistor [tolerance=±5% resistance=3.3k package=THT]
  R28 = Resistor [tolerance=±5% resistance=3.3k package=THT]
  R29 = Resistor [tolerance=±5% resistance=1.5k package=THT]
  R30 = Resistor [tolerance=±5% resistance=1.5k package=THT]
  R31 = Resistor [tolerance=±5% resistance=1.5k package=THT]
  J25 = female pin header, 4 pins [form="♀ (female)"]
  J26 = female pin header, 4 pins [form="♀ (female)"]
  C7 = Ceramic Capacitor [capacitance=0.1µF package="100 mil [THT, multilayer]"]  # not connected
  C3 = Electrolytic Capacitor [capacitance=47µF voltage=35V package="100 mil [THT, electrolytic]"]  # not connected
  C8 = Ceramic Capacitor [capacitance=0.1µF package="100 mil [THT, multilayer]"]  # not connected

nets:
  N1: J1.pin1, R8.Pin_0
  N2: J2.pin1, R7.Pin_0
  N3: J3.pin1, R6.Pin_0
  N4: J4.pin1, R5.Pin_0
  N5: J5.pin1, R9.Pin_0
  N6: J6.pin1, R10.Pin_1
  N7: J7.pin1, R4.Pin_1
  N8: J8.pin1, R3.Pin_1
  N9: J9.pin1, R2.Pin_1
  N10: J10.pin1, R1.Pin_1
  N11: J11.pin1, R16.Pin_1
  N12: J12.pin1, R15.Pin_0
  N13: J13.pin1, R13.Pin_0
  N14: J14.pin1, R12.Pin_0
  N15: J15.pin1, R11.Pin_1
  N16: J16.pin1, R14.Pin_1
  N17: R1.Pin_0, B12.pin1
  N18: R2.Pin_0, B8.pin1
  N19: R3.Pin_0, B4.pin1
  N20: R4.Pin_0, B0.pin1
  N21: R5.Pin_1, B15.pin1
  N22: R6.Pin_1, B11.pin1
  N23: R7.Pin_1, B7.pin1
  N24: R8.Pin_1, B3.pin1
  N25: R9.Pin_1, B2.pin1
  N26: R10.Pin_0, B1.pin1
  N27: R11.Pin_0, B5.pin1
  N28: R12.Pin_1, B6.pin1
  N29: R13.Pin_1, B10.pin1
  N30: R14.Pin_0, B9.pin1
  N31: R15.Pin_1, B14.pin1
  N32: R16.Pin_0, B13.pin1
  N33: J22.pin2, Q2.B
  N34: J22.pin3, Q3.B
  N35: J22.pin4, Q4.B
  N36: U1.RESET, R17.Pin_0
  N37: U1.D4, R18.Pin_1
  N38: U1.VCC, R17.Pin_1
  N39: U1.GND, C2.1, J26.pin2
  N40: U1.D5_(PWM), R19.Pin_1
  N41: U1.D6_(PWM), R20.Pin_1
  N42: U1.D7, R21.Pin_1
  N43: U1.D10_(PWM), R31.Pin_1
  N44: U1.D11_(PWM), R30.Pin_1
  N45: U1.D12, J24.pin7
  N46: U1.D13, R29.Pin_1
  N47: U1.A1, U3.SH_CP
  N48: U1.A2, U2.DS
  N49: U2.Q7', U3.DS
  N50: U2.ST_CP, U3.ST_CP
  VCC: U2.VCC, U3.MR, U3.VCC, J24.pin4, Q5.source
  N51: Q1.E, J24.pin6
  N52: Q1.C, R18.Pin_0
  N53: Q2.C, R19.Pin_0
  N54: Q3.C, R20.Pin_0
  N55: Q4.C, R21.Pin_0
  N56: J24.pin5, R29.Pin_0
  N57: Q5.gate, J25.pin3
  N58: R27.Pin_1, R30.Pin_0
  N59: R28.Pin_1, R31.Pin_0
